# Fritzing sketch aqua-sensor-circuit (saved by Fritzing 0.9.3b)
circuit board: 6.28603cm x 7.42423cm

parts:
  Part1 = Arduino Pro Mini v13
  Part2 = NRF24L01+ Breakout Board
  J1 = female pin header, 3 pins [form="♀ (female)"]
  J2 = female pin header, 4 pins [form="♀ (female)"]
  J3 = female pin header, 3 pins [form="♀ (female)"]
  J4 = female pin header, 2 pins [form="♀ (female)"]
  J5 = female pin header, 3 pins [form="♀ (female)"]
  R1 = Resistor [tolerance=±5% resistance=1k package=THT]
  C1 = Ceramic Capacitor [capacitance=10nF package="200 mil [THT, multilayer]"]
  C2 = Ceramic Capacitor [capacitance=10nF package="200 mil [THT, multilayer]"]
  R2 = Resistor [tolerance=±5% resistance=1k package=THT]
  R3 = Resistor [tolerance=±5% resistance=1k package=THT]
  C3 = Ceramic Capacitor [capacitance=10nF package="200 mil [THT, multilayer]"]

nets:
  N1: Part1.VCC, J1.pin1, J3.pin1, J5.pin1, R1.Pin_1, R2.Pin_1, R3.Pin_0
  GND: Part1.GND, Part2.GND, J1.pin2, J3.pin3, J4.pin2, J5.pin2, C1.1, C2.1, C3.1
  N2: Part1.D13/SCK, Part2.SCK
  N3: Part1.D12/MISO, Part2.MISO
  N4: Part1.D11_PWM/MOSI, Part2.MOSI
  N5: Part1.D10_PWM/SS, Part2.CS
  N6: Part1.D9_PWM, Part2.CE
  N7: Part1.D8, J2.pin1
  N8: Part1.D7, J2.pin2
  N9: Part1.D6_PWM, J2.pin3
  N10: Part1.D5_PWM, J2.pin4
  N11: Part1.D4, J4.pin1, C1.0, R2.Pin_0
  N12: Part1.D3_PWM, J1.pin3, C2.0, R3.Pin_1
  N13: Part1.D2, J5.pin3, R1.Pin_0, C3.0
  N14: Part2.VCC, J3.pin2
